// Logisim project atividade_logisim_final.circ as structural Verilog: 2 circuits, main circuit main
module main (
  input  [2:0] A,
  input  [2:0] B
);

  wire and_1_out, and_2_out, and_3_out, and_4_out, and_5_out, clock_1_out, conversor3para7_1_a,
       conversor3para7_1_b, conversor3para7_1_c, conversor3para7_1_d, conversor3para7_1_e,
       conversor3para7_1_f, conversor3para7_1_g, or_1_out, xor_2_out, xor_4_out;
  wire [2:0] register_1_q, xor_1_out;

  xor xor_1 (xor_1_out[0], A[0], B[0]);
  and and_1 (and_1_out, A[0], B[0]);
  xor xor_2 (xor_2_out, A[1], B[1]);
  xor xor_3 (xor_1_out[1], xor_2_out, and_1_out);
  and and_2 (and_2_out, xor_2_out, and_1_out);
  and and_3 (and_3_out, A[1], B[1]);
  xor xor_4 (xor_4_out, A[2], B[2]);
  or or_1 (or_1_out, and_2_out, and_3_out);
  xor xor_5 (xor_1_out[2], xor_4_out, or_1_out);
  and and_4 (and_4_out, or_1_out, xor_4_out);
  and and_5 (and_5_out, A[2], B[2]);
  // OR_Gate or_2 has open pins: in0=and_5_out, in1=and_4_out, out=open
  Register #(.width(3)) register_1 (.D(xor_1_out), .en(1'b1), .clk(clock_1_out), .Q(register_1_q));  // open: clr
  Clock clock_1 (.out(clock_1_out));
  Conversor3para7 conversor3para7_1 (
    .A2(register_1_q[2]), .A1(register_1_q[1]), .A0(register_1_q[0]), .a(conversor3para7_1_a),
    .b(conversor3para7_1_b), .c(conversor3para7_1_c), .d(conversor3para7_1_d), .e(conversor3para7_1_e),
    .f(conversor3para7_1_f), .g(conversor3para7_1_g));
  _7_Segment_Display u_7_segment_display_1 (
    .g(conversor3para7_1_g), .f(conversor3para7_1_f), .a(conversor3para7_1_a), .b(conversor3para7_1_b),
    .e(conversor3para7_1_e), .d(conversor3para7_1_d), .c(conversor3para7_1_c));  // open: dp
endmodule

module Conversor3para7 (
  input  A2,
  input  A1,
  input  A0,
  output a,
  output b,
  output c,
  output d,
  output e,
  output f,
  output g
);

  wire and_1_out, and_2_out, and_3_out, and_4_out, and_5_out, and_6_out, and_7_out, and_8_out, and_9_out,
       and_10_out, and_11_out, and_12_out, and_13_out, and_14_out, and_15_out, and_16_out, not_1_out,
       not_2_out, not_3_out;

  not not_1 (not_1_out, A2);
  not not_2 (not_2_out, A1);
  not not_3 (not_3_out, A0);
  and and_1 (and_1_out, not_1_out, not_3_out);
  and and_2 (and_2_out, A2, A0);
  and and_3 (and_3_out, not_2_out, not_3_out);
  and and_4 (and_4_out, A1, A0);
  or or_1 (c, not_2_out, A0, A2);
  and and_5 (and_5_out, not_1_out, not_3_out);
  and and_6 (and_6_out, not_1_out, A1);
  and and_7 (and_7_out, A2, not_2_out, A0);
  and and_8 (and_8_out, A1, not_3_out);
  and and_9 (and_9_out, not_1_out, not_3_out);
  and and_10 (and_10_out, A1, not_3_out);
  and and_11 (and_11_out, not_2_out, not_3_out);
  and and_12 (and_12_out, A2, not_2_out);
  and and_13 (and_13_out, A2, not_3_out);
  and and_14 (and_14_out, not_1_out, A1);
  and and_15 (and_15_out, A2, not_2_out);
  and and_16 (and_16_out, A1, not_3_out);
  or or_2 (a, and_1_out, A1, and_2_out);
  or or_3 (b, not_1_out, and_3_out, and_4_out);
  or or_4 (d, and_5_out, and_6_out, and_7_out, and_8_out);
  or or_5 (e, and_9_out, and_10_out);
  or or_6 (f, and_11_out, and_12_out, and_13_out);
  or or_7 (g, and_14_out, and_15_out, and_16_out);
endmodule
